# Fritzing sketch lasertag (saved by Fritzing 1.0.0rc)
breadboards: 1

parts:
  Grove1 = Grove OLED 128x96  # not connected
  IC1 = ULN2003A [package="DIP16 [THT]"]  # not connected
  J1 = Piezo Speaker
  IR1 = TSOP312.., 314.. [package=THT]
  LED1 = LEDs [package=led10mm]
  Mod1 = Amica NodeMCU DEVKIT 1.0
  S1 = SWITCH-MOMENTARY-2 [package=tactile-pth-12mm]
  R1 = Resistor [tolerance=±5% power=0.25W resistance=220 package=THT]
  LED2 = smd LED [color="Red (633nm)" package="1206 [SMD]"]
  LED3 = smd LED [color="Blue (525nm)" package="1206 [SMD]"]

nets:
  N1: J1.pin2, IR1.GND, LED1.A, Mod1.pin_30, R1.Pin_1, LED2.anode, LED3.anode
  N2: IR1.Vs, Mod1.pin_12
  N3: IR1.Data, Mod1.pin2, Mod1.pin_9, Mod1.pin_25, Mod1.pin_29
  N4: Mod1.pin1, Mod1.pin_10, Mod1.pin_26
  N5: Mod1.pin_11, S1.2, R1.Pin_0

notes:
  You can power the entire board either through the MicroUSB port on the NodeMCU module or via the VCC and GND pins.
